# Fritzing sketch DataMonsterCircuitry (saved by Fritzing 0.8.3b)
breadboards: 1

parts:
  R1 = Resistor [tolerance=±5% resistance=220 package=THT]
  LED1 = LED - 5mm [color="Red (633nm)" package="5 mm [THT]"]
  R2 = Resistor [tolerance=±5% resistance=220 package=THT]
  LED2 = LED - 5mm [color="Yellow (585nm)" package="5 mm [THT]"]
  R3 = Resistor [tolerance=±5% resistance=220 package=THT]
  LED3 = LED - 5mm [color="Green (560nm)" package="5 mm [THT]"]
  S1 = Pushbutton [package="[THT]"]
  R4 = Resistor [tolerance=±5% resistance=10k package=THT]
  C1 = Ceramic Capacitor [capacitance=10µF package="100 mil [THT, multilayer]"]
  Power_plug1 = Power plug
  J1 = Basic Servo
  J2 = Basic Servo
  J3 = Basic Servo
  J4 = Basic Servo
  J5 = Basic Servo
  J6 = Infrared Proximity Sensor
  J7 = Infrared Proximity Sensor
  J8 = Infrared Proximity Sensor
  LED4 = Red LED - 5mm [package="5 mm [THT]"]  # not connected

nets:
  N1: R1.Pin_0, LED1.cathode
  GND: R1.Pin_1, R2.Pin_1, R3.Pin_1, R4.Pin_1, C1.0, Power_plug1.GND, J1.gnd, J2.gnd, J3.gnd, J4.gnd, J5.gnd, J6.GND, J7.GND, J8.GND
  N2: R2.Pin_0, LED2.cathode
  N3: R3.Pin_0, LED3.cathode
  VCC: S1.Pin_1, S1.Pin_2, R4.Pin_0, C1.1, J6.Vcc, J7.Vcc, J8.Vcc
  N4: S1.Pin_3, S1.Pin_4
  VCC_2: Power_plug1.VCC, J1.vcc, J2.vcc, J3.vcc, J4.vcc, J5.vcc

custom parts:
  Red LED - 5mm: A generic red LED (~1.8V)
